// Logisim project B2_Group2_Simulation.circ as structural Verilog: 1 circuit, main circuit main
module main (
  input  B4,
  input  B3,
  input  B2,
  input  B1,
  input  A4,
  input  A3,
  input  A2,
  input  A1,
  input  CS2,
  input  CS1,
  input  CS0,
  output F4,
  output F3,
  output F2,
  output F1,
  output C,
  output S,
  output Z,
  output V
);

  wire adder_1_cout, adder_2_cout, adder_3_cout, adder_4_cout, and_1_out, and_2_out, and_3_out, and_4_out,
       and_5_out, and_6_out, and_7_out, and_8_out, not_1_out, not_2_out, not_3_out, not_4_out, not_5_out,
       not_6_out, or_1_out, or_2_out, or_3_out, or_4_out, or_5_out, or_6_out, or_7_out, or_8_out, or_9_out,
       or_10_out, xnor_1_out, xnor_2_out, xnor_3_out, xnor_4_out;

  not not_1 (not_1_out, CS2);
  not not_2 (not_2_out, CS1);
  not not_3 (not_3_out, B1);
  not not_4 (not_4_out, B2);
  not not_5 (not_5_out, B3);
  not not_6 (not_6_out, B4);
  and and_1 (and_1_out, CS2, not_2_out, not_3_out);
  xnor xnor_1 (xnor_1_out, CS1, CS2);
  and and_2 (and_2_out, CS2, not_2_out, not_4_out);
  xnor xnor_2 (xnor_2_out, CS1, CS2);
  and and_3 (and_3_out, CS2, not_2_out, not_5_out);
  xnor xnor_3 (xnor_3_out, CS1, CS2);
  and and_4 (and_4_out, CS2, not_2_out, not_6_out);
  xnor xnor_4 (xnor_4_out, CS1, CS2);
  or or_1 (or_1_out, A1, and_1_out);
  or or_2 (or_2_out, not_3_out, xnor_1_out);
  or or_3 (or_3_out, A2, and_2_out);
  or or_4 (or_4_out, not_4_out, xnor_2_out);
  or or_5 (or_5_out, A3, and_3_out);
  or or_6 (or_6_out, not_5_out, xnor_3_out);
  or or_7 (or_7_out, A4, and_4_out);
  or or_8 (or_8_out, not_6_out, xnor_4_out);
  and and_5 (and_5_out, not_1_out, CS0);
  Adder #(.width(1)) adder_1 (.a(or_1_out), .b(or_2_out), .out(F1), .cin(and_5_out), .cout(adder_1_cout));
  and and_6 (and_6_out, not_1_out, adder_1_cout);
  Adder #(.width(1)) adder_2 (.a(or_3_out), .b(or_4_out), .out(F2), .cin(and_6_out), .cout(adder_2_cout));
  and and_7 (and_7_out, not_1_out, adder_2_cout);
  Adder #(.width(1)) adder_3 (.a(or_5_out), .b(or_6_out), .out(F3), .cin(and_7_out), .cout(adder_3_cout));
  and and_8 (and_8_out, not_1_out, adder_3_cout);
  Adder #(.width(1)) adder_4 (.a(or_7_out), .b(or_8_out), .out(F4), .cin(and_8_out), .cout(adder_4_cout));
  and and_9 (C, not_1_out, adder_4_cout);
  xor xor_1 (V, C, and_8_out);
  or or_9 (or_9_out, F1, F2);
  or or_10 (or_10_out, F4, F3);
  nor nor_1 (Z, or_9_out, or_10_out);

  assign S = F4;
endmodule
