// Logisim project B2_Group2_Offline_2_circuit.circ as structural Verilog: 6 circuits, main circuit main
module main (
  input  [15:0] Input1,
  input  [15:0] Input1_2,
  output [15:0] Output,
  output Underflow,
  output Overflow
);

  FPA FPA (.Input1(Input1), .Input1_2(Input1_2), .Output(Output), .Underflow(Underflow), .Overflow(Overflow));
endmodule

module FPA (
  input  [15:0] Input1,
  input  [15:0] Input1_2,
  output [15:0] Output,
  output Underflow,
  output Overflow
);

  wire comparator_1_eq;
  wire [3:0] Normalizer_exponent_output, Splitter_output_exponent;
  wire [11:0] Normalizer_normalized_significand;
  wire [13:0] adder_1_out, Splitter_significand1, Splitter_significand2;
  wire [15:15] Normalizer_sign_output;

  Splitter Splitter (
    .Input1(Input1), .Input2(Input1_2), .Significand1(Splitter_significand1),
    .Significand2(Splitter_significand2), .Output_Exponent(Splitter_output_exponent));
  Adder #(.width(14)) adder_1 (
    .a(Splitter_significand1), .b(Splitter_significand2), .out(adder_1_out));  // open: cin, cout
  Normalizer Normalizer (
    .Significand(adder_1_out), .Exponent(Splitter_output_exponent),
    .Normalized_Significand(Normalizer_normalized_significand), .Exponent_Output(Normalizer_exponent_output),
    .Sign_Output(Normalizer_sign_output[15]));
  Comparator #(.width(14)) comparator_1 (.a(adder_1_out), .b({14{1'b0}}), .eq(comparator_1_eq));  // open: gt, lt
  nor nor_1 (Underflow, Normalizer_exponent_output[0], Normalizer_exponent_output[1], Normalizer_exponent_output[2], Normalizer_exponent_output[3]);
  and and_1 (Overflow, Normalizer_exponent_output[0], Normalizer_exponent_output[1], Normalizer_exponent_output[2], Normalizer_exponent_output[3]);
  Multiplexer #(.width(16), .enable("false")) multiplexer_1 (
    .in0({Normalizer_sign_output[15], Normalizer_exponent_output, Normalizer_normalized_significand[10:0]}),
    .in1({16{1'b0}}), .out(Output), .sel(comparator_1_eq));
endmodule

module Splitter (
  input  [15:0] Input1,
  input  [15:0] Input2,
  output [13:0] Significand1,
  output [13:0] Significand2,
  output [3:0] Output_Exponent
);

  wire subtractor_1_bout;
  wire [3:0] multiplexer_1_out, multiplexer_2_out, negator_1_out, subtractor_1_out;
  wire [11:0] shifter_1_out, shifter_2_out;

  Multiplexer #(.width(4), .enable("false")) multiplexer_1 (
    .in0(4'b0000), .in1(negator_1_out), .out(multiplexer_1_out), .sel(subtractor_1_bout));
  Negator_part #(.width(4)) negator_1 (.in(subtractor_1_out), .out(negator_1_out));
  Subtractor #(.width(4)) subtractor_1 (
    .a(Input1[14:11]), .b(Input2[14:11]), .out(subtractor_1_out), .bout(subtractor_1_bout));  // open: bin
  Multiplexer #(.width(4), .enable("false")) multiplexer_2 (
    .in0(subtractor_1_out), .in1(4'b0000), .out(multiplexer_2_out), .sel(subtractor_1_bout));
  Shifter #(.width(12), .shift("lr")) shifter_1 (
    .in({1'b1, Input1[10:0]}), .\dist (multiplexer_1_out), .out(shifter_1_out));
  Multiplexer #(.width(4), .enable("false")) multiplexer_3 (
    .in0(Input1[14:11]), .in1(Input2[14:11]), .out(Output_Exponent), .sel(subtractor_1_bout));
  Shifter #(.width(12), .shift("lr")) shifter_2 (
    .in({1'b1, Input2[10:0]}), .\dist (multiplexer_2_out), .out(shifter_2_out));
  Negator minus_x_14bit (._12bit_Number(shifter_1_out), .Sign(Input1[15]), ._14bit_Output_Number(Significand1));
  Negator minus_x_14bit_2 (._12bit_Number(shifter_2_out), .Sign(Input2[15]), ._14bit_Output_Number(Significand2));
endmodule

module Negator (
  input  [11:0] _12bit_Number,
  input  Sign,
  output [13:0] _14bit_Output_Number
);

  wire [13:0] negator_1_out;

  Negator_part #(.width(14)) negator_1 (.in({2'b00, _12bit_Number}), .out(negator_1_out));
  Multiplexer #(.width(14), .enable("false")) multiplexer_1 (
    .in0({2'b00, _12bit_Number}), .in1(negator_1_out), .out(_14bit_Output_Number), .sel(Sign));
endmodule

module Normalizer (
  input  [13:0] Significand,
  input  [3:0] Exponent,
  output [11:0] Normalized_Significand,
  output [3:0] Exponent_Output,
  output Sign_Output
);

  wire [3:0] adder_1_out, Shift_Counter_count, subtractor_1_out;
  wire [11:0] shifter_2_out;
  wire [12:0] shifter_1_out;
  wire [13:0] multiplexer_1_out, negator_1_out;

  Negator_part #(.width(14)) negator_1 (.in(Significand), .out(negator_1_out));
  Multiplexer #(.width(14), .enable("false")) multiplexer_1 (
    .in0(Significand), .in1(negator_1_out), .out(multiplexer_1_out), .sel(Significand[13]));
  Shifter #(.width(13), .shift("lr")) shifter_1 (.in(multiplexer_1_out[12:0]), .\dist (4'b0001), .out(shifter_1_out));
  ShiftCounter Shift_Counter (.Input(multiplexer_1_out[11:0]), .Count(Shift_Counter_count));
  Multiplexer #(.select(2), .width(12), .enable("false")) multiplexer_2 (
    .in0(shifter_2_out), .in1(multiplexer_1_out[11:0]), .in2(shifter_1_out[11:0]), .in3(shifter_1_out[11:0]),
    .out(Normalized_Significand), .sel(multiplexer_1_out[12:11]));
  Adder #(.width(4)) adder_1 (.a(Exponent), .b(4'b0001), .out(adder_1_out));  // open: cin, cout
  Shifter #(.width(12)) shifter_2 (.in(multiplexer_1_out[11:0]), .\dist (Shift_Counter_count), .out(shifter_2_out));
  Subtractor #(.width(4)) subtractor_1 (
    .a(Exponent), .b(Shift_Counter_count), .out(subtractor_1_out));  // open: bin, bout
  Multiplexer #(.select(2), .width(4), .enable("false")) multiplexer_3 (
    .in0(subtractor_1_out), .in1(Exponent), .in2(adder_1_out), .in3(adder_1_out), .out(Exponent_Output),
    .sel(multiplexer_1_out[12:11]));

  assign Sign_Output = Significand[13];
endmodule

module ShiftCounter (
  input  [11:0] Input,
  output [3:0] Count
);

  wire priority_encoder_1_gs;
  wire [3:0] priority_encoder_1_out, subtractor_1_out;

  Priority_Encoder #(.select(4)) priority_encoder_1 (
    .in0(Input[0]), .in1(Input[1]), .in2(Input[2]), .in3(Input[3]), .in4(Input[4]), .in5(Input[5]),
    .in6(Input[6]), .in7(Input[7]), .in8(Input[8]), .in9(Input[9]), .in10(Input[10]), .in11(Input[11]),
    .in12(1'b0), .in13(1'b0), .in14(1'b0), .in15(1'b0), .out(priority_encoder_1_out),
    .gs(priority_encoder_1_gs));  // open: en_out, en_in
  Subtractor #(.width(4)) subtractor_1 (
    .a(4'b1011), .b(priority_encoder_1_out), .out(subtractor_1_out));  // open: bin, bout
  Multiplexer #(.width(4), .enable("false")) multiplexer_1 (
    .in0(4'b0000), .in1(subtractor_1_out), .out(Count), .sel(priority_encoder_1_gs));
endmodule
