// Logisim project Group2_B2_Offline_3_8_Bit_MIPS_regfile_output_shown.circ as structural Verilog: 5 circuits, main circuit 8-Bit MIPS
module _8_Bit_MIPS (
  output [7:0] zero,
  output [7:0] t0,
  output [7:0] t1,
  output [7:0] t2,
  output [7:0] t3,
  output [7:0] t4,
  output [7:0] sp
);

  wire and_1_out, and_2_out, Clock_out, control_1_brancheq, control_1_branchneq, control_1_jump,
       control_1_memread, control_1_memtoreg, control_1_memwrite, control_1_regdst, control_1_regwrite,
       n8_bit_alu_1_zf, not_1_out, or_1_out, Reset_out;
  wire [1:0] control_1_alusrc;
  wire [2:0] control_1_aluop;
  wire [3:0] multiplexer_1_out;
  wire [7:0] adder_1_out, adder_2_out, data_memory_1_read_data, multiplexer_2_out, multiplexer_3_out,
       multiplexer_4_out, multiplexer_5_out, n8_bit_alu_1_alu_output, PC_q, register_file_1_read_data_1,
       register_file_1_read_data_2, rom_1_data_2;
  wire [19:0] rom_1_data;

  Clock Clock (.out(Clock_out));
  Button Reset (.out(Reset_out));
  Register #(.trigger("falling")) PC (.D(multiplexer_4_out), .Q(PC_q), .clk(Clock_out), .clr(Reset_out));  // open: en
  Adder adder_1 (.a(PC_q), .b(8'h1), .out(adder_1_out), .cin(1'b0));  // open: cout
  ROM #(.dataWidth(20)) rom_1 (.addr(PC_q), .data({rom_1_data[19:16], rom_1_data_2, rom_1_data[7:0]}));  // open: sel
  Control control_1 (
    .Opcode(rom_1_data[19:16]), .RegDst(control_1_regdst), .Jump(control_1_jump),
    .BranchEq(control_1_brancheq), .BranchNeq(control_1_branchneq), .MemRead(control_1_memread),
    .MemtoReg(control_1_memtoreg), .ALUOp(control_1_aluop), .MemWrite(control_1_memwrite),
    .ALUSrc(control_1_alusrc), .RegWrite(control_1_regwrite));
  Multiplexer #(.width(4), .enable("false")) multiplexer_1 (
    .in0(rom_1_data_2[3:0]), .in1(rom_1_data[7:4]), .out(multiplexer_1_out), .sel(control_1_regdst));
  Register_File register_file_1 (
    .Write_register(multiplexer_1_out), .Write_data(multiplexer_5_out),
    .Read_data_1(register_file_1_read_data_1), .Read_data_2(register_file_1_read_data_2),
    .Read_register_2(rom_1_data_2[3:0]), .Read_register_1(rom_1_data_2[7:4]), .RegWrite(control_1_regwrite),
    .Clock(Clock_out), .Clear(Reset_out), .zero(zero), .t0(t0), .t1(t1), .t2(t2), .t3(t3), .t4(t4), .sp(sp));
  Adder adder_2 (.a(adder_1_out), .b(rom_1_data[7:0]), .out(adder_2_out), .cin(1'b0));  // open: cout
  Multiplexer #(.select(2), .width(8), .enable("false")) multiplexer_2 (
    .in0(register_file_1_read_data_2), .in1({4'b0000, rom_1_data[3:0]}), .in2(rom_1_data[7:0]),
    .out(multiplexer_2_out), .sel(control_1_alusrc));  // open: in3
  _8_Bit_ALU u_8_bit_alu_1 (
    .A(register_file_1_read_data_1), .B(multiplexer_2_out), .ALU_Op(control_1_aluop), .ZF(n8_bit_alu_1_zf),
    .ALU_Output(n8_bit_alu_1_alu_output));  // open: out_4, out_5
  Multiplexer #(.width(8), .enable("false")) multiplexer_3 (
    .in0(adder_1_out), .in1(adder_2_out), .out(multiplexer_3_out), .sel(or_1_out));
  or or_1 (or_1_out, and_1_out, and_2_out);
  and and_1 (and_1_out, control_1_brancheq, n8_bit_alu_1_zf);
  and and_2 (and_2_out, control_1_branchneq, not_1_out);
  not not_1 (not_1_out, n8_bit_alu_1_zf);
  Data_Memory data_memory_1 (
    .Address(n8_bit_alu_1_alu_output), .Write_data(register_file_1_read_data_2),
    .Read_data(data_memory_1_read_data), .MemWrite(control_1_memwrite), .MemRead(control_1_memread),
    .Clock(Clock_out), .Clear(Reset_out));
  Multiplexer #(.width(8), .enable("false")) multiplexer_4 (
    .in0(multiplexer_3_out), .in1(rom_1_data_2), .out(multiplexer_4_out), .sel(control_1_jump));
  Multiplexer #(.width(8), .enable("false")) multiplexer_5 (
    .in0(n8_bit_alu_1_alu_output), .in1(data_memory_1_read_data), .out(multiplexer_5_out),
    .sel(control_1_memtoreg));

  // Notes on the sheet:
  //   contents of rom_1 (hex, n*v repeats v):
  //   8020a 80305 2310 1340 4150 b3203 f2021 a4201 41d00 95150 52202 e4041 d3203 22410 c1530 41c00 56601
  //   b6100 56601 b6300 31105 d6100 86601 63314 d6300 86601 13330 41d00 731f3
endmodule

// ALU
module _8_Bit_ALU (
  input  [7:0] A,
  input  [7:0] B,
  input  [2:0] ALU_Op,
  output out_4,
  output out_5,
  output ZF,
  output [7:0] ALU_Output
);

  wire [7:0] adder_1_out, and_1_out, nor_1_out, or_1_out, subtractor_1_out;
  wire [15:0] shifter_1_out, shifter_2_out;

  Adder adder_1 (.a(A), .b(B), .out(adder_1_out), .cin(1'b0), .cout(out_4));
  Subtractor subtractor_1 (.a(A), .b(B), .out(subtractor_1_out), .bin(1'b0), .bout(out_5));
  assign and_1_out = A & B;  // AND_Gate and_1, 8 bits wide
  assign or_1_out = A | B;  // OR_Gate or_1, 8 bits wide
  assign nor_1_out = ~(A | B);  // NOR_Gate nor_1, 8 bits wide
  Shifter #(.width(16)) shifter_1 (.in({{8{1'b0}}, A}), .\dist (B[3:0]), .out(shifter_1_out));
  Shifter #(.width(16), .shift("lr")) shifter_2 (.in({{8{1'b0}}, A}), .\dist (B[3:0]), .out(shifter_2_out));
  Multiplexer #(.select(3), .width(8), .enable("false")) multiplexer_1 (
    .in0(adder_1_out), .in1(subtractor_1_out), .in2(and_1_out), .in3(or_1_out), .in4(nor_1_out),
    .in5(shifter_1_out[7:0]), .in6(shifter_2_out[7:0]), .in7({8{1'b1}}), .out(ALU_Output), .sel(ALU_Op));
  nor nor_2 (ZF, ALU_Output[0], ALU_Output[1], ALU_Output[2], ALU_Output[3], ALU_Output[4], ALU_Output[5], ALU_Output[6], ALU_Output[7]);
endmodule

module Control (
  input  [3:0] Opcode,
  output RegDst,
  output Jump,
  output BranchEq,
  output BranchNeq,
  output MemRead,
  output MemtoReg,
  output [2:0] ALUOp,
  output MemWrite,
  output [1:0] ALUSrc,
  output RegWrite
);

  wire [15:13] rom_1_data;

  ROM #(.addrWidth(4), .dataWidth(16)) rom_1 (
    .addr(Opcode),
    .data({rom_1_data, RegWrite, ALUSrc, MemWrite, ALUOp, MemtoReg, MemRead, BranchNeq, BranchEq, Jump, RegDst}));  // open: sel

  // Notes on the sheet:
  //   contents of rom_1 (hex, n*v repeats v):
  //   1001 1101 1081 18c0 2 1840 1880 48 1800 1041 44 a00 10c1 1830 1581 1541
endmodule

// Registers
module Register_File (
  input  [3:0] Read_register_1,
  input  [3:0] Read_register_2,
  input  [3:0] Write_register,
  input  [7:0] Write_data,
  input  RegWrite,
  input  Clock,
  input  Clear,
  output [7:0] zero,
  output [7:0] t0,
  output [7:0] t1,
  output [7:0] t2,
  output [7:0] t3,
  output [7:0] t4,
  output [7:0] sp,
  output [7:0] Read_data_1,
  output [7:0] Read_data_2
);

  wire decoder_1_out0, decoder_1_out1, decoder_1_out2, decoder_1_out3, decoder_1_out4, decoder_1_out5,
       decoder_1_out6;

  Decoder #(.select(4), .disabled(0)) decoder_1 (
    .out0(decoder_1_out0), .out1(decoder_1_out1), .out2(decoder_1_out2), .out3(decoder_1_out3),
    .out4(decoder_1_out4), .out5(decoder_1_out5), .out6(decoder_1_out6), .sel(Write_register), .en(RegWrite));  // open: out7, out8, out9, out10, out11, out12, out13, out14, out15
  Register u_zero (.D({8{1'b0}}), .en(decoder_1_out0), .Q(zero), .clk(Clock), .clr(Clear));
  Register u_t0 (.D(Write_data), .en(decoder_1_out1), .Q(t0), .clk(Clock), .clr(Clear));
  Register u_t1 (.D(Write_data), .en(decoder_1_out2), .Q(t1), .clk(Clock), .clr(Clear));
  Register u_t2 (.D(Write_data), .en(decoder_1_out3), .Q(t2), .clk(Clock), .clr(Clear));
  Register u_t3 (.D(Write_data), .en(decoder_1_out4), .Q(t3), .clk(Clock), .clr(Clear));
  Register u_t4 (.D(Write_data), .en(decoder_1_out5), .Q(t4), .clk(Clock), .clr(Clear));
  Register u_sp (.D(Write_data), .en(decoder_1_out6), .Q(sp), .clk(Clock), .clr(Clear));
  Multiplexer #(.select(4), .width(8), .enable("false")) multiplexer_1 (
    .in0(zero), .in1(t0), .in2(t1), .in3(t2), .in4(t3), .in5(t4), .in6(sp), .out(Read_data_1),
    .sel(Read_register_1));  // open: in7, in8, in9, in10, in11, in12, in13, in14, in15
  Multiplexer #(.select(4), .width(8), .enable("false")) multiplexer_2 (
    .in0(zero), .in1(t0), .in2(t1), .in3(t2), .in4(t3), .in5(t4), .in6(sp), .out(Read_data_2),
    .sel(Read_register_2));  // open: in7, in8, in9, in10, in11, in12, in13, in14, in15
endmodule

module Data_Memory (
  input  [7:0] Address,
  input  [7:0] Write_data,
  input  MemWrite,
  input  MemRead,
  input  Clock,
  input  Clear,
  output [7:0] Read_data
);

  RAM #(.bus("separate")) ram_1 (
    .addr(Address), .din(Write_data), .data(Read_data), .str(MemWrite), .clk(Clock), .ld(MemRead), .clr(Clear));  // open: sel
endmodule
