// Logisim project Group2_B2_Offline_4_8_Bit_MIPS_pipelined.circ as structural Verilog: 9 circuits, main circuit 8-Bit MIPS Pipelined
module _8_Bit_MIPS_Pipelined (
  output [7:0] zero,
  output [7:0] t0,
  output [7:0] t1,
  output [7:0] t2,
  output [7:0] t3,
  output [7:0] t4,
  output [7:0] sp
);

  wire Clock_out, Reset_out;
  wire [0:0] EX_MEM_output;
  wire [1:0] forward_unit_1_forwarda, forward_unit_1_forwardb;
  wire [2:0] control_1_aluop;
  wire [3:0] EX_MEM_output_3;
  wire [7:0] adder_1_out, EX_MEM_output_2, MEM_WB_output_2, multiplexer_1_out, multiplexer_2_out,
       n8_bit_alu_1_alu_output, PC_q;
  wire [12:0] MEM_WB_output;
  wire [19:0] IF_ID_output, rom_1_data;
  wire [31:0] control_1_regwrite, ID_EX_output;

  Button Reset (.out(Reset_out));
  Clock Clock (.out(Clock_out));
  Register PC (.D(adder_1_out), .Q(PC_q), .clk(Clock_out), .clr(Reset_out));  // open: en
  Adder adder_1 (.a(PC_q), .b(8'h1), .out(adder_1_out), .cin(1'b0));  // open: cout
  ROM #(.dataWidth(20)) rom_1 (.addr(PC_q), .data(rom_1_data));  // open: sel
  _20_Bit_Register IF_ID (
    .Input(rom_1_data),
    .Output({IF_ID_output[19:16], control_1_regwrite[23:20], control_1_regwrite[27:24], control_1_regwrite[31:28], IF_ID_output[3:0]}),
    .Clock(Clock_out));
  Control control_1 (
    .Opcode(IF_ID_output[19:16]), .ALUOp(control_1_aluop), .RegWrite(control_1_regwrite[0]));  // open: RegDst, Jump, BranchEq, BranchNeq, MemRead, MemtoReg, MemWrite, ALUSrc
  Register_File register_file_1 (
    .Write_register(MEM_WB_output[12:9]), .Write_data(MEM_WB_output_2), .Clock(Clock_out), .Clear(Reset_out),
    .zero(zero), .t0(t0), .t1(t1), .t2(t2), .t3(t3), .t4(t4), .sp(sp),
    .Read_data_1(control_1_regwrite[11:4]), .Read_data_2(control_1_regwrite[19:12]),
    .Read_register_2(control_1_regwrite[27:24]), .Read_register_1(control_1_regwrite[23:20]));  // open: RegWrite
  _32_Bit_Register ID_EX (
    .Input({control_1_regwrite[31:4], control_1_aluop, control_1_regwrite[0]}), .Output(ID_EX_output),
    .Clock(Clock_out));
  Multiplexer #(.select(2), .width(8), .enable("false")) multiplexer_1 (
    .in0(ID_EX_output[19:12]), .in1(MEM_WB_output_2), .in2(EX_MEM_output_2), .out(multiplexer_1_out),
    .sel(forward_unit_1_forwardb));  // open: in3
  Multiplexer #(.select(2), .width(8), .enable("false")) multiplexer_2 (
    .in0(ID_EX_output[11:4]), .in1(MEM_WB_output_2), .in2(EX_MEM_output_2), .out(multiplexer_2_out),
    .sel(forward_unit_1_forwarda));  // open: in3
  _8_Bit_ALU u_8_bit_alu_1 (
    .A(multiplexer_2_out), .B(multiplexer_1_out), .ALU_Op(ID_EX_output[3:1]),
    .ALU_Output(n8_bit_alu_1_alu_output));  // open: ZF, out_4, out_5
  Forward_Unit forward_unit_1 (
    .EX_MEM_RegWrite(EX_MEM_output[0]), .EX_MEM_RegisterRd(EX_MEM_output_3),
    .ID_EX_RegisterRs(ID_EX_output[23:20]), .ID_EX_RegisterRt(ID_EX_output[27:24]),
    .MEM_WB_RegWrite(MEM_WB_output[0]), .MEM_WB_RegisterRd(MEM_WB_output[12:9]),
    .ForwardA(forward_unit_1_forwarda), .ForwardB(forward_unit_1_forwardb));
  _13_Bit_Register EX_MEM (
    .Input({ID_EX_output[31:28], n8_bit_alu_1_alu_output, ID_EX_output[0]}),
    .Output({EX_MEM_output_3, EX_MEM_output_2, EX_MEM_output[0]}), .Clock(Clock_out));
  Data_Memory data_memory_1 (
    .Clock(Clock_out), .Clear(Reset_out));  // open: Address, Write_data, Read_data, MemWrite, MemRead
  _13_Bit_Register MEM_WB (
    .Input({EX_MEM_output_3, EX_MEM_output_2, EX_MEM_output[0]}),
    .Output({MEM_WB_output[12:9], MEM_WB_output_2, MEM_WB_output[0]}), .Clock(Clock_out));

  // Notes on the sheet:
  //   contents of rom_1 (hex, n*v repeats v):
  //   3420 92350 c2450 5450
endmodule

module Register_File (
  input  [3:0] Read_register_1,
  input  [3:0] Read_register_2,
  input  [3:0] Write_register,
  input  [7:0] Write_data,
  input  RegWrite,
  input  Clock,
  input  Clear,
  output [7:0] zero,
  output [7:0] t0,
  output [7:0] t1,
  output [7:0] t2,
  output [7:0] t3,
  output [7:0] t4,
  output [7:0] sp,
  output [7:0] Read_data_1,
  output [7:0] Read_data_2
);

  wire decoder_1_out0, decoder_1_out1, decoder_1_out2, decoder_1_out3, decoder_1_out4, decoder_1_out5,
       decoder_1_out6;

  Decoder #(.select(4), .disabled(0)) decoder_1 (
    .out0(decoder_1_out0), .out1(decoder_1_out1), .out2(decoder_1_out2), .out3(decoder_1_out3),
    .out4(decoder_1_out4), .out5(decoder_1_out5), .out6(decoder_1_out6), .sel(Write_register), .en(RegWrite));  // open: out7, out8, out9, out10, out11, out12, out13, out14, out15
  Register u_zero (.D({8{1'b0}}), .en(decoder_1_out0), .Q(zero), .clk(Clock), .clr(Clear));
  Register u_t0 (.D(Write_data), .en(decoder_1_out1), .Q(t0), .clk(Clock), .clr(Clear));
  Register u_t1 (.D(Write_data), .en(decoder_1_out2), .Q(t1), .clk(Clock), .clr(Clear));
  Register u_t2 (.D(Write_data), .en(decoder_1_out3), .Q(t2), .clk(Clock), .clr(Clear));
  Register u_t3 (.D(Write_data), .en(decoder_1_out4), .Q(t3), .clk(Clock), .clr(Clear));
  Register u_t4 (.D(Write_data), .en(decoder_1_out5), .Q(t4), .clk(Clock), .clr(Clear));
  Register u_sp (.D(Write_data), .en(decoder_1_out6), .Q(sp), .clk(Clock), .clr(Clear));
  Multiplexer #(.select(4), .width(8), .enable("false")) multiplexer_1 (
    .in0(zero), .in1(t0), .in2(t1), .in3(t2), .in4(t3), .in5(t4), .in6(sp), .out(Read_data_1),
    .sel(Read_register_1));  // open: in7, in8, in9, in10, in11, in12, in13, in14, in15
  Multiplexer #(.select(4), .width(8), .enable("false")) multiplexer_2 (
    .in0(zero), .in1(t0), .in2(t1), .in3(t2), .in4(t3), .in5(t4), .in6(sp), .out(Read_data_2),
    .sel(Read_register_2));  // open: in7, in8, in9, in10, in11, in12, in13, in14, in15
endmodule

module Control (
  input  [3:0] Opcode,
  output RegDst,
  output Jump,
  output BranchEq,
  output BranchNeq,
  output MemRead,
  output MemtoReg,
  output [2:0] ALUOp,
  output MemWrite,
  output [1:0] ALUSrc,
  output RegWrite
);

  wire [15:13] rom_1_data;

  ROM #(.addrWidth(4), .dataWidth(16)) rom_1 (
    .addr(Opcode),
    .data({rom_1_data, RegWrite, ALUSrc, MemWrite, ALUOp, MemtoReg, MemRead, BranchNeq, BranchEq, Jump, RegDst}));  // open: sel

  // Notes on the sheet:
  //   contents of rom_1 (hex, n*v repeats v):
  //   1001 1101 1081 18c0 2 1840 1880 48 1800 1041 44 a00 10c1 1830 1581 1541
endmodule

// ALU
module _8_Bit_ALU (
  input  [7:0] A,
  input  [7:0] B,
  input  [2:0] ALU_Op,
  output out_4,
  output out_5,
  output ZF,
  output [7:0] ALU_Output
);

  wire [7:0] adder_1_out, and_1_out, nor_1_out, or_1_out, subtractor_1_out;
  wire [15:0] shifter_1_out, shifter_2_out;

  Adder adder_1 (.a(A), .b(B), .out(adder_1_out), .cin(1'b0), .cout(out_4));
  Subtractor subtractor_1 (.a(A), .b(B), .out(subtractor_1_out), .bin(1'b0), .bout(out_5));
  assign and_1_out = A & B;  // AND_Gate and_1, 8 bits wide
  assign or_1_out = A | B;  // OR_Gate or_1, 8 bits wide
  assign nor_1_out = ~(A | B);  // NOR_Gate nor_1, 8 bits wide
  Shifter #(.width(16)) shifter_1 (.in({{8{1'b0}}, A}), .\dist (B[3:0]), .out(shifter_1_out));
  Shifter #(.width(16), .shift("lr")) shifter_2 (.in({{8{1'b0}}, A}), .\dist (B[3:0]), .out(shifter_2_out));
  Multiplexer #(.select(3), .width(8), .enable("false")) multiplexer_1 (
    .in0(adder_1_out), .in1(subtractor_1_out), .in2(and_1_out), .in3(or_1_out), .in4(nor_1_out),
    .in5(shifter_1_out[7:0]), .in6(shifter_2_out[7:0]), .in7({8{1'b1}}), .out(ALU_Output), .sel(ALU_Op));
  nor nor_2 (ZF, ALU_Output[0], ALU_Output[1], ALU_Output[2], ALU_Output[3], ALU_Output[4], ALU_Output[5], ALU_Output[6], ALU_Output[7]);
endmodule

module Forward_Unit (
  input  EX_MEM_RegWrite,
  input  [3:0] EX_MEM_RegisterRd,
  input  [3:0] ID_EX_RegisterRs,
  input  [3:0] ID_EX_RegisterRt,
  input  MEM_WB_RegWrite,
  input  [3:0] MEM_WB_RegisterRd,
  output [1:0] ForwardA,
  output [1:0] ForwardB
);

  wire comparator_1_eq, comparator_2_eq, comparator_3_eq, comparator_4_eq, comparator_5_eq, comparator_6_eq,
       not_1_out, not_2_out, not_3_out, not_4_out;

  Comparator #(.width(4)) comparator_1 (.a(4'b0000), .b(EX_MEM_RegisterRd), .eq(comparator_1_eq));  // open: gt, lt
  Comparator #(.width(4)) comparator_2 (
    .a(EX_MEM_RegisterRd), .b(ID_EX_RegisterRs), .eq(comparator_2_eq));  // open: gt, lt
  Comparator #(.width(4)) comparator_3 (
    .a(EX_MEM_RegisterRd), .b(ID_EX_RegisterRt), .eq(comparator_3_eq));  // open: gt, lt
  Comparator #(.width(4)) comparator_4 (.a(4'b0000), .b(MEM_WB_RegisterRd), .eq(comparator_4_eq));  // open: gt, lt
  Comparator #(.width(4)) comparator_5 (
    .a(MEM_WB_RegisterRd), .b(ID_EX_RegisterRs), .eq(comparator_5_eq));  // open: gt, lt
  Comparator #(.width(4)) comparator_6 (
    .a(MEM_WB_RegisterRd), .b(ID_EX_RegisterRt), .eq(comparator_6_eq));  // open: gt, lt
  not not_1 (not_1_out, comparator_1_eq);
  not not_2 (not_2_out, comparator_4_eq);
  and and_1 (ForwardA[1], EX_MEM_RegWrite, not_1_out, comparator_2_eq);
  and and_2 (ForwardB[1], EX_MEM_RegWrite, not_1_out, comparator_3_eq);
  not not_3 (not_3_out, ForwardA[1]);
  not not_4 (not_4_out, ForwardB[1]);
  and and_3 (ForwardA[0], not_3_out, MEM_WB_RegWrite, not_2_out, comparator_5_eq);
  and and_4 (ForwardB[0], not_4_out, MEM_WB_RegWrite, not_2_out, comparator_6_eq);
endmodule

module _13_Bit_Register (
  input  [12:0] Input,
  input  Clock,
  output [12:0] Output
);

  Register #(.width(13)) PC (.D(Input), .Q(Output), .clk(Clock));  // open: en, clr
endmodule

module _20_Bit_Register (
  input  [19:0] Input,
  input  Clock,
  output [19:0] Output
);

  Register #(.width(20)) PC (.D(Input), .Q(Output), .clk(Clock));  // open: en, clr
endmodule

module _32_Bit_Register (
  input  [31:0] Input,
  input  Clock,
  output [31:0] Output
);

  Register #(.width(32)) PC (.D(Input), .Q(Output), .clk(Clock));  // open: en, clr
endmodule

module Data_Memory (
  input  [7:0] Address,
  input  [7:0] Write_data,
  input  MemWrite,
  input  MemRead,
  input  Clock,
  input  Clear,
  output [7:0] Read_data
);

  RAM #(.bus("separate")) ram_1 (
    .addr(Address), .din(Write_data), .data(Read_data), .str(MemWrite), .clk(Clock), .ld(MemRead), .clr(Clear));  // open: sel
endmodule
